# Fritzing sketch blinkenlights-lab (saved by Fritzing 0.3.14b)
breadboards: 1

parts:
  Freeduino = Arduino
  470Ω = Resistor [resistance=560 package=THT]
  LED = Red LED - 5mm
  green = green LED - 5mm
  470Ω_2 = Resistor [resistance=560 package=THT]
  470Ω_3 = Resistor [resistance=560 package=THT]
  blue = Blue LED - 5mm

nets:
  N1: Freeduino.GND, 470Ω.Pin_1, 470Ω_2.Pin_1, 470Ω_3.Pin_1
  N2: Freeduino.D11, LED.anode
  N3: Freeduino.D6, blue.anode
  N4: Freeduino.D3, green.anode
  N5: 470Ω.Pin_0, LED.cathode
  N6: green.cathode, 470Ω_3.Pin_0
  N7: 470Ω_2.Pin_0, blue.cathode

notes:
  Your Linear Slide Potentiometer
