# Fritzing sketch ch2-one-led-circuit (saved by Fritzing 0.3.14b)
breadboards: 1

parts:
  part = Arduino
  470_ohm = Resistor [resistance=470 package=THT]
  LED = white LED - 5mm
  LED_2 = Red LED - 5mm

nets:
  N1: part.GND, 470_ohm.Pin_1
  N2: part.D13, LED.anode, LED_2.anode
  N3: 470_ohm.Pin_0, LED.cathode, LED_2.cathode

notes:
  From pin 13 to the LED, through the resistor, and back to GND.
