# Fritzing sketch ch3-two-led-circuit (saved by Fritzing 0.3.14b)
breadboards: 1

parts:
  part = Arduino
  470_ohm = Resistor [resistance=470 package=THT]
  LED = green LED - 5mm
  470_ohm_2 = Resistor [resistance=470 package=THT]
  LED_2 = Red LED - 5mm

nets:
  N1: part.GND, 470_ohm.Pin_1, 470_ohm_2.Pin_1
  N2: part.D12, LED_2.anode
  N3: part.D11, LED.anode
  N4: 470_ohm.Pin_0, LED_2.cathode
  N5: LED.cathode, 470_ohm_2.Pin_0

notes:
  Use the ground rail to connect all your LEDs to ground.
