# Fritzing sketch ch4-button-circuit (saved by Fritzing 0.3.14b)
breadboards: 1

parts:
  Arduino1 = Arduino
  S1 = Pushbutton [package="[THT]"]
  R1 = Resistor [resistance=10k package=THT]
  R2 = Resistor [resistance=220 package=THT]
  LED1 = Red LED - 5mm

nets:
  N1: Arduino1.GND, R1.Pin_1, R2.Pin_1
  N2: Arduino1.D12, LED1.anode
  N3: Arduino1.D2, S1.Pin_1, S1.Pin_2, R1.Pin_0
  N4: Arduino1.+5V, S1.Pin_3, S1.Pin_4
  N5: R2.Pin_0, LED1.cathode
